// Logisim project SingleCycle.circ as structural Verilog
module alu (
  input  [4:0] ALU_Control,
  input  [31:0] in_2,
  input  [31:0] in_3,
  output Branch,
  output [31:0] out_5
);

  wire comparator_1_eq, comparator_1_gt, comparator_1_lt, comparator_2_eq, comparator_2_gt, comparator_2_lt,
       comparator_3_eq, comparator_3_lt, comparator_4_eq, comparator_5_eq, not_1_out, or_2_out, or_3_out;
  wire [31:0] adder_1_out, and_1_out, multiplexer_1_out, multiplexer_2_out, multiplexer_3_out,
       multiplexer_4_out, multiplexer_5_out, multiplexer_6_out, multiplexer_7_out, or_1_out, shifter_1_out,
       shifter_2_out, shifter_3_out, subtractor_1_out, xor_1_out;

  Adder #(.width(32)) adder_1 (.a(in_2), .b(in_3), .out(adder_1_out));  // open: cin, cout
  Shifter #(.width(32)) shifter_1 (.in(in_2), .\dist (in_3[4:0]), .out(shifter_1_out));
  Comparator #(.width(32)) comparator_1 (
    .a(in_2), .b(in_3), .gt(comparator_1_gt), .eq(comparator_1_eq), .lt(comparator_1_lt));
  assign xor_1_out = in_2 ^ in_3;  // XOR_Gate xor_1, 32 bits wide
  Shifter #(.width(32), .shift("lr")) shifter_2 (.in(in_2), .\dist (in_3[4:0]), .out(shifter_2_out));
  assign or_1_out = in_2 | in_3;  // OR_Gate or_1, 32 bits wide
  assign and_1_out = in_2 & in_3;  // AND_Gate and_1, 32 bits wide
  Subtractor #(.width(32)) subtractor_1 (.a(in_2), .b(in_3), .out(subtractor_1_out));  // open: bin, bout
  Shifter #(.width(32), .shift("ar")) shifter_3 (.in(in_2), .\dist (in_3[4:0]), .out(shifter_3_out));
  Comparator #(.width(32), .mode("unsigned")) comparator_2 (
    .a(in_2), .b(in_3), .gt(comparator_2_gt), .eq(comparator_2_eq), .lt(comparator_2_lt));
  Comparator #(.width(32)) comparator_3 (.a(in_2), .b(in_3), .eq(comparator_3_eq), .lt(comparator_3_lt));  // open: gt
  or or_2 (or_2_out, comparator_1_eq, comparator_1_gt);
  or or_3 (or_3_out, comparator_2_gt, comparator_2_eq);
  not not_1 (not_1_out, comparator_3_eq);
  Multiplexer #(.width(32), .enable("false")) multiplexer_1 (
    .in0({32{1'b0}}), .in1(32'h1), .out(multiplexer_1_out), .sel(not_1_out));
  Multiplexer #(.width(32), .enable("false")) multiplexer_2 (
    .in0({32{1'b0}}), .in1(32'h1), .out(multiplexer_2_out), .sel(comparator_1_lt));
  Multiplexer #(.width(32), .enable("false")) multiplexer_3 (
    .in0({32{1'b0}}), .in1(32'h1), .out(multiplexer_3_out), .sel(comparator_1_eq));
  Multiplexer #(.width(32), .enable("false")) multiplexer_4 (
    .in0({32{1'b0}}), .in1(32'h1), .out(multiplexer_4_out), .sel(or_2_out));
  Multiplexer #(.width(32), .enable("false")) multiplexer_5 (
    .in0({32{1'b0}}), .in1(32'h1), .out(multiplexer_5_out), .sel(comparator_2_lt));
  Multiplexer #(.width(32), .enable("false")) multiplexer_6 (
    .in0({32{1'b0}}), .in1(32'h1), .out(multiplexer_6_out), .sel(or_3_out));
  Multiplexer #(.width(32), .enable("false")) multiplexer_7 (
    .in0({32{1'b0}}), .in1(32'h1), .out(multiplexer_7_out), .sel(comparator_3_lt));
  Multiplexer #(.select(5), .width(32), .disabled(0), .enable("false")) multiplexer_8 (
    .in0(adder_1_out), .in1(shifter_1_out), .in2(multiplexer_2_out), .in3(multiplexer_5_out),
    .in4(xor_1_out), .in5(shifter_2_out), .in6(or_1_out), .in7(and_1_out), .in8(subtractor_1_out),
    .in13(shifter_3_out), .in16(multiplexer_3_out), .in17(multiplexer_1_out), .in20(multiplexer_7_out),
    .in21(multiplexer_4_out), .in22(multiplexer_5_out), .in23(multiplexer_6_out), .in31(in_2), .out(out_5),
    .sel(ALU_Control));  // open: in9, in10, in11, in12, in14, in15, in18, in19, in24, in25, in26, in27, in28, in29, in30
  Comparator #(.width(2), .mode("unsigned")) comparator_4 (
    .a(ALU_Control[4:3]), .b(2'b10), .eq(comparator_4_eq));  // open: gt, lt
  Comparator #(.width(32), .mode("unsigned")) comparator_5 (
    .a(32'h1), .b(out_5), .eq(comparator_5_eq));  // open: gt, lt
  and and_2 (Branch, comparator_4_eq, comparator_5_eq);

  // Notes on the sheet:
  //   A
  //   B
  //   ADD,ADDI
  //   SLL,SLLI
  //   OR,ORI
  //    AND,ANDI
  //   SUB
  //   SRA,SRAI
  //   XOR,XORI
  //   SRL,SRLI
  //   SLT,SLTI
  //   BEQ
  //   SLTU,SLTUI,BLTU
  //   BGEU
  //   BNE
  //   JAL,JALR
  //   BGE
  //   BLT
  //   Output
endmodule

module RISC_V (
);

  wire alu_1_branch, and_1_out, clock_1_out, control_1_out_2, control_1_out_3, control_1_out_4,
       control_1_out_5, control_1_out_6, control_1_out_9, Restart_Program_out, Zero_Reg_File_out;
  wire [1:0] control_1_out_8, control_1_out_10, control_1_out_11;
  wire [2:0] control_1_out_7;
  wire [4:0] alu_control_1_out_4;
  wire [31:0] adder_1_out, alu_1_out_5, immediate_generation_1_out_3, immediate_generation_1_out_4,
       immediate_generation_1_out_5, immediate_generation_1_out_6, immediate_generation_1_out_7,
       jalr_target_1_out_3, multiplexer_1_out, multiplexer_2_out, multiplexer_3_out, multiplexer_4_out,
       multiplexer_5_out, multiplexer_6_out, ram_1_data, reg_32_1_readdata1, reg_32_1_readdata2,
       register_1_q, rom_1_data;

  Register #(.width(32), .Select("low")) register_1 (
    .D(multiplexer_1_out), .Q(register_1_q), .clk(clock_1_out), .clr(Restart_Program_out));  // open: en
  Button Restart_Program (.out(Restart_Program_out));
  Button Zero_Reg_File (.out(Zero_Reg_File_out));
  Adder #(.width(32)) adder_1 (.a(register_1_q), .b(32'h4), .out(adder_1_out));  // open: cin, cout
  Clock clock_1 (.out(clock_1_out));
  Multiplexer #(.select(2), .width(32), .enable("false")) multiplexer_1 (
    .in0(adder_1_out), .in1(multiplexer_2_out), .in2(immediate_generation_1_out_6),
    .in3(jalr_target_1_out_3), .out(multiplexer_1_out), .sel(control_1_out_11));
  ROM #(.addrWidth(20), .dataWidth(32), .Select("high")) rom_1 (.addr(register_1_q[21:2]), .data(rom_1_data));
  Multiplexer #(.width(32), .enable("false")) multiplexer_2 (
    .in0(adder_1_out), .in1(immediate_generation_1_out_4), .out(multiplexer_2_out), .sel(and_1_out));
  Immediate_Generation immediate_generation_1 (
    .in_1(rom_1_data), .out_4(immediate_generation_1_out_4), .out_5(immediate_generation_1_out_5),
    .out_6(immediate_generation_1_out_6), .out_3(immediate_generation_1_out_3),
    .out_7(immediate_generation_1_out_7), .in_2(register_1_q));
  control control_1 (
    .in_1(rom_1_data[6:0]), .out_2(control_1_out_2), .out_3(control_1_out_3), .out_4(control_1_out_4),
    .out_5(control_1_out_5), .out_6(control_1_out_6), .out_7(control_1_out_7), .out_8(control_1_out_8),
    .out_9(control_1_out_9), .out_10(control_1_out_10), .out_11(control_1_out_11));
  reg_32 reg_32_1 (
    .ReadReg1(rom_1_data[19:15]), .ReadReg2(rom_1_data[24:20]), .WriteReg(rom_1_data[11:7]),
    .RegWrite(control_1_out_5), .ReadData1(reg_32_1_readdata1), .ReadData2(reg_32_1_readdata2),
    .WriteData(multiplexer_6_out), .Clk(clock_1_out), .Reset(Zero_Reg_File_out));
  and and_1 (and_1_out, alu_1_branch, control_1_out_3);
  JALR_target jalr_target_1 (.in_1(reg_32_1_readdata1), .in_2(multiplexer_3_out), .out_3(jalr_target_1_out_3));
  Multiplexer #(.select(2), .width(32), .enable("false")) multiplexer_3 (
    .in0(immediate_generation_1_out_7), .in1(immediate_generation_1_out_3),
    .in2(immediate_generation_1_out_5), .out(multiplexer_3_out), .sel(control_1_out_10));  // open: in3
  ALU_CONTROL alu_control_1 (
    .out_4(alu_control_1_out_4), .ALUOp(control_1_out_7), .Func_3(rom_1_data[14:12]), .Func_7(rom_1_data[30]));
  Multiplexer #(.select(2), .width(32), .enable("false")) multiplexer_4 (
    .in0(reg_32_1_readdata1), .in1(adder_1_out), .in2(register_1_q), .in3(reg_32_1_readdata1),
    .out(multiplexer_4_out), .sel(control_1_out_8));
  Multiplexer #(.width(32), .enable("false")) multiplexer_5 (
    .in0(reg_32_1_readdata2), .in1(multiplexer_3_out), .out(multiplexer_5_out), .sel(control_1_out_9));
  alu alu_1 (
    .out_5(alu_1_out_5), .in_2(multiplexer_4_out), .ALU_Control(alu_control_1_out_4), .Branch(alu_1_branch),
    .in_3(multiplexer_5_out));
  RAM #(.dataWidth(32), .bus("separate"), .Select("high"), .simpleMode("false")) ram_1 (
    .addr(alu_1_out_5[9:2]), .din(reg_32_1_readdata2), .data(ram_1_data), .str(control_1_out_2),
    .clk(clock_1_out), .ld(control_1_out_4));  // open: sel, clr
  Multiplexer #(.width(32), .enable("false")) multiplexer_6 (
    .in0(alu_1_out_5), .in1(ram_1_data), .out(multiplexer_6_out));  // open: sel

  // Notes on the sheet:
  //   Clock
endmodule

module instruction_type_decode (
  input  [6:0] opcode,
  output R_format,
  output Load,
  output Store,
  output Branch,
  output I_Type,
  output JALR,
  output JAL,
  output LUI
);

  Comparator #(.width(7), .mode("unsigned")) comparator_1 (.a(7'b0110011), .b(opcode), .eq(R_format));  // open: gt, lt
  Comparator #(.width(7), .mode("unsigned")) comparator_2 (.a(7'b0000011), .b(opcode), .eq(Load));  // open: gt, lt
  Comparator #(.width(7), .mode("unsigned")) comparator_3 (.a(7'b0100011), .b(opcode), .eq(Store));  // open: gt, lt
  Comparator #(.width(7), .mode("unsigned")) comparator_4 (.a(7'b1100011), .b(opcode), .eq(Branch));  // open: gt, lt
  Comparator #(.width(7), .mode("unsigned")) comparator_5 (.a(7'b0010011), .b(opcode), .eq(I_Type));  // open: gt, lt
  Comparator #(.width(7), .mode("unsigned")) comparator_6 (.a(7'b1100111), .b(opcode), .eq(JALR));  // open: gt, lt
  Comparator #(.width(7), .mode("unsigned")) comparator_7 (.a(7'b1101111), .b(opcode), .eq(JAL));  // open: gt, lt
  Comparator #(.width(7), .mode("unsigned")) comparator_8 (.a(7'b0110111), .b(opcode), .eq(LUI));  // open: gt, lt
endmodule

module control_decode (
  input  Rformat,
  input  Load,
  input  Store,
  input  Branch,
  input  l_Type,
  input  JALR,
  input  JAL,
  input  Lui,
  output MenWrite,
  output Branch_2,
  output MemRead,
  output RegWrite,
  output MemtoReg,
  output [2:0] ALUoperation,
  output [1:0] operand_A_sel,
  output operand_B_sel,
  output [1:0] extend_sel,
  output [1:0] next_PC_sel
);

  or or_1 (RegWrite, Rformat, Load, l_Type, Lui, JAL, JALR);
  ALUop aluop_1 (
    .R_Type(Rformat), .Load(Load), .Store(Store), .Branch(Branch), .I_Type(l_Type), .JALR(JALR), .JAL(JAL),
    .LUI(Lui), .out_9(ALUoperation));
  operand_A_sel operand_a_sel_1 (.LUI(Lui), .JALR(JALR), .JAL(JAL), .out_4(operand_A_sel));
  or or_2 (operand_B_sel, Lui, l_Type, Store, Load);
  next_pc_sel next_pc_sel_1 (.b(Branch), .j(JAL), .jr(JALR), .out_4(next_PC_sel));

  assign Branch_2 = Branch;
  assign extend_sel = {Store, Lui};
  assign MemRead = Load;
  assign MemtoReg = Load;
  assign MenWrite = Store;
endmodule

module ALU_CONTROL (
  input  [2:0] ALUOp,
  input  Func_7,
  input  [2:0] Func_3,
  output [4:0] out_4
);

  wire and_1_out, and_2_out, and_3_out, and_4_out, and_5_out, and_6_out, and_7_out, and_8_out, and_9_out,
       and_10_out, and_11_out, not_1_out, not_2_out, not_3_out, not_4_out, not_5_out, not_6_out, not_7_out,
       not_8_out, not_9_out, not_10_out, not_11_out, not_12_out, not_13_out, not_14_out, not_15_out,
       not_16_out, not_17_out, not_18_out, not_19_out, not_20_out, not_21_out, not_22_out, not_23_out,
       not_24_out;
  wire [3:0] priority_encoder_1_out;

  and and_1 (and_1_out, ALUOp[0], not_1_out, ALUOp[1]);
  not not_1 (not_1_out, ALUOp[2]);
  not not_2 (not_2_out, ALUOp[2]);
  and and_2 (and_2_out, not_2_out, ALUOp[1], not_3_out);
  not not_3 (not_3_out, ALUOp[0]);
  not not_4 (not_4_out, ALUOp[2]);
  not not_5 (not_5_out, ALUOp[1]);
  and and_3 (and_3_out, not_4_out, not_5_out, not_6_out, not_7_out);
  not not_6 (not_6_out, ALUOp[0]);
  not not_7 (not_7_out, Func_7);
  not not_8 (not_8_out, ALUOp[1]);
  not not_9 (not_9_out, ALUOp[0]);
  and and_4 (and_4_out, not_8_out, not_9_out, Func_7, not_10_out);
  not not_10 (not_10_out, ALUOp[2]);
  not not_11 (not_11_out, ALUOp[2]);
  not not_12 (not_12_out, ALUOp[1]);
  and and_5 (and_5_out, not_11_out, not_12_out, ALUOp[0]);
  not not_13 (not_13_out, Func_3[1]);
  and and_6 (and_6_out, Func_3[2], not_13_out, Func_3[0]);
  not not_14 (not_14_out, ALUOp[2]);
  not not_15 (not_15_out, ALUOp[1]);
  not not_16 (not_16_out, Func_7);
  and and_7 (and_7_out, and_5_out, not_16_out, and_6_out);
  and and_8 (and_8_out, and_5_out, and_6_out, Func_7);
  and and_9 (and_9_out, and_5_out, and_6_out);
  and and_10 (and_10_out, not_14_out, not_15_out, ALUOp[0]);
  not not_17 (not_17_out, and_1_out);
  not not_18 (not_18_out, and_2_out);
  not not_19 (not_19_out, and_3_out);
  not not_20 (not_20_out, and_4_out);
  and and_11 (and_11_out, not_17_out, not_18_out, not_19_out, not_20_out, not_21_out, not_22_out, not_23_out, not_24_out);
  not not_21 (not_21_out, and_7_out);
  not not_22 (not_22_out, and_8_out);
  not not_23 (not_23_out, and_9_out);
  not not_24 (not_24_out, and_10_out);
  Priority_Encoder #(.select(4)) priority_encoder_1 (
    .in0(and_1_out), .in1(and_2_out), .in2(and_3_out), .in3(and_4_out), .in5(and_7_out), .in6(and_8_out),
    .in7(and_9_out), .in8(and_10_out), .in9(and_11_out), .out(priority_encoder_1_out));  // open: in4, in10, in11, in12, in13, in14, in15, gs, en_out, en_in
  Multiplexer #(.select(4), .width(5), .enable("false")) multiplexer_1 (
    .in0({5{1'b1}}), .in1({2'b10, Func_3}), .in2({2'b00, Func_3}), .in3({2'b01, Func_3}),
    .in4({2'b00, Func_3}), .in6({2'b01, Func_3}), .in7({2'b00, Func_3}), .in8({2'b00, Func_3}),
    .in9({5{1'b0}}), .out(out_4), .sel(priority_encoder_1_out));  // open: in5, in10, in11, in12, in13, in14, in15
endmodule

module control (
  input  [6:0] in_1,
  output out_2,
  output out_3,
  output out_4,
  output out_5,
  output out_6,
  output [2:0] out_7,
  output [1:0] out_8,
  output out_9,
  output [1:0] out_10,
  output [1:0] out_11
);

  wire instruction_type_decode_1_branch, instruction_type_decode_1_i_type, instruction_type_decode_1_jal,
       instruction_type_decode_1_jalr, instruction_type_decode_1_load, instruction_type_decode_1_lui,
       instruction_type_decode_1_r_format, instruction_type_decode_1_store;

  instruction_type_decode instruction_type_decode_1 (
    .opcode(in_1), .R_format(instruction_type_decode_1_r_format), .Load(instruction_type_decode_1_load),
    .Store(instruction_type_decode_1_store), .Branch(instruction_type_decode_1_branch),
    .I_Type(instruction_type_decode_1_i_type), .JALR(instruction_type_decode_1_jalr),
    .JAL(instruction_type_decode_1_jal), .LUI(instruction_type_decode_1_lui));
  control_decode control_decode_1 (
    .Rformat(instruction_type_decode_1_r_format), .Load(instruction_type_decode_1_load),
    .Store(instruction_type_decode_1_store), .Branch(instruction_type_decode_1_branch), .MenWrite(out_2),
    .Branch_2(out_3), .MemRead(out_4), .MemtoReg(out_6), .l_Type(instruction_type_decode_1_i_type),
    .JALR(instruction_type_decode_1_jalr), .JAL(instruction_type_decode_1_jal), .operand_A_sel(out_8),
    .extend_sel(out_10), .Lui(instruction_type_decode_1_lui), .ALUoperation(out_7), .operand_B_sel(out_9),
    .next_PC_sel(out_11), .RegWrite(out_5));

  // Notes on the sheet:
  //   Instruction OpCode
endmodule

module reg_32 (
  input  [4:0] ReadReg1,
  input  [4:0] ReadReg2,
  input  [4:0] WriteReg,
  input  RegWrite,
  input  [31:0] WriteData,
  input  Clk,
  input  Reset,
  output [31:0] ReadData1,
  output [31:0] ReadData2
);

  wire decoder_1_out0, decoder_1_out1, decoder_2_out0, decoder_2_out1, decoder_2_out2, decoder_2_out3,
       decoder_3_out0, decoder_3_out1, decoder_3_out2, decoder_3_out3, decoder_4_out0, decoder_4_out1,
       decoder_4_out2, decoder_4_out3, decoder_5_out0, decoder_5_out1, decoder_5_out2, decoder_5_out3,
       decoder_6_out0, decoder_6_out1, decoder_6_out2, decoder_6_out3, decoder_7_out0, decoder_7_out1,
       decoder_7_out2, decoder_7_out3, decoder_8_out0, decoder_8_out1, decoder_8_out2, decoder_8_out3,
       decoder_9_out0, decoder_9_out1, decoder_9_out2, decoder_9_out3, decoder_10_out0, decoder_10_out1,
       decoder_10_out2, decoder_10_out3, decoder_11_out0, decoder_11_out1, decoder_11_out2, decoder_11_out3;
  wire [31:0] multiplexer_1_out, multiplexer_2_out, multiplexer_3_out, multiplexer_4_out, multiplexer_5_out,
       multiplexer_6_out, multiplexer_7_out, multiplexer_8_out, multiplexer_9_out, multiplexer_10_out,
       multiplexer_13_out, multiplexer_14_out, multiplexer_15_out, multiplexer_16_out, multiplexer_17_out,
       multiplexer_18_out, multiplexer_19_out, multiplexer_20_out, multiplexer_21_out, multiplexer_22_out,
       register_1_q, register_2_q, register_3_q, register_4_q, register_5_q, register_6_q, register_7_q,
       register_8_q, register_9_q, register_10_q, register_11_q, register_12_q, register_13_q, register_14_q,
       register_15_q, register_16_q, register_17_q, register_18_q, register_19_q, register_20_q,
       register_21_q, register_22_q, register_23_q, register_24_q, register_25_q, register_26_q,
       register_27_q, register_28_q, register_29_q, register_30_q, register_31_q;

  // Probe on WriteReg
  Decoder #(.disabled(0)) decoder_1 (.out0(decoder_1_out0), .out1(decoder_1_out1), .sel(WriteReg[4]), .en(RegWrite));
  Decoder #(.select(2), .disabled(0)) decoder_2 (
    .out0(decoder_2_out0), .out1(decoder_2_out1), .out2(decoder_2_out2), .out3(decoder_2_out3),
    .sel(WriteReg[3:2]), .en(decoder_1_out0));
  Decoder #(.select(2), .disabled(0)) decoder_3 (
    .out0(decoder_3_out0), .out1(decoder_3_out1), .out2(decoder_3_out2), .out3(decoder_3_out3),
    .sel(WriteReg[1:0]), .en(decoder_2_out0));
  Decoder #(.select(2), .disabled(0)) decoder_4 (
    .out0(decoder_4_out0), .out1(decoder_4_out1), .out2(decoder_4_out2), .out3(decoder_4_out3),
    .sel(WriteReg[1:0]), .en(decoder_2_out1));
  Decoder #(.select(2), .disabled(0)) decoder_5 (
    .out0(decoder_5_out0), .out1(decoder_5_out1), .out2(decoder_5_out2), .out3(decoder_5_out3),
    .sel(WriteReg[1:0]), .en(decoder_2_out2));
  Decoder #(.select(2), .disabled(0)) decoder_6 (
    .out0(decoder_6_out0), .out1(decoder_6_out1), .out2(decoder_6_out2), .out3(decoder_6_out3),
    .sel(WriteReg[1:0]), .en(decoder_2_out3));
  Register #(.width(32), .Select("low")) register_1 (
    .D(WriteData), .en(decoder_3_out1), .Q(register_1_q), .clk(Clk), .clr(Reset));
  Register #(.width(32), .Select("low")) register_2 (
    .D(WriteData), .en(decoder_3_out2), .Q(register_2_q), .clk(Clk), .clr(Reset), .preset(Reset));  // open: cs
  Register #(.width(32), .Select("low")) register_3 (
    .D(WriteData), .en(decoder_3_out3), .Q(register_3_q), .clk(Clk), .clr(Reset), .preset(Reset));  // open: cs
  Register #(.width(32), .Select("low")) register_4 (
    .D(WriteData), .en(decoder_4_out0), .Q(register_4_q), .clk(Clk), .clr(Reset), .preset(Reset));  // open: cs
  Register #(.width(32), .Select("low")) register_5 (
    .D(WriteData), .en(decoder_4_out1), .Q(register_5_q), .clk(Clk), .clr(Reset), .preset(Reset));  // open: cs
  Register #(.width(32), .Select("low")) register_6 (
    .D(WriteData), .en(decoder_4_out2), .Q(register_6_q), .clk(Clk), .clr(Reset), .preset(Reset));  // open: cs
  Register #(.width(32), .Select("low")) register_7 (
    .D(WriteData), .en(decoder_4_out3), .Q(register_7_q), .clk(Clk), .clr(Reset), .preset(Reset));  // open: cs
  Register #(.width(32), .Select("low")) register_8 (
    .D(WriteData), .en(decoder_5_out0), .Q(register_8_q), .clk(Clk), .clr(Reset), .preset(Reset));  // open: cs
  Register #(.width(32), .Select("low")) register_9 (
    .D(WriteData), .en(decoder_5_out1), .Q(register_9_q), .clk(Clk), .clr(Reset), .preset(Reset));  // open: cs
  Register #(.width(32), .Select("low")) register_10 (
    .D(WriteData), .en(decoder_5_out2), .Q(register_10_q), .clk(Clk), .clr(Reset), .preset(Reset));  // open: cs
  Register #(.width(32), .Select("low")) register_11 (
    .D(WriteData), .en(decoder_5_out3), .Q(register_11_q), .clk(Clk), .clr(Reset), .preset(Reset));  // open: cs
  Register #(.width(32), .Select("low")) register_12 (
    .D(WriteData), .en(decoder_6_out0), .Q(register_12_q), .clk(Clk), .clr(Reset), .preset(Reset));  // open: cs
  Register #(.width(32), .Select("low")) register_13 (
    .D(WriteData), .en(decoder_6_out1), .Q(register_13_q), .clk(Clk), .clr(Reset), .preset(Reset));  // open: cs
  Register #(.width(32), .Select("low")) register_14 (
    .D(WriteData), .en(decoder_6_out2), .Q(register_14_q), .clk(Clk), .clr(Reset), .preset(Reset));  // open: cs
  Register #(.width(32), .Select("low")) register_15 (
    .D(WriteData), .en(decoder_6_out3), .Q(register_15_q), .clk(Clk), .clr(Reset), .preset(Reset));  // open: cs
  // Probe on {32{1'b0}}
  // Probe on register_1_q
  // Probe on register_2_q
  // Probe on register_3_q
  // Probe on register_4_q
  // Probe on register_5_q
  // Probe on register_6_q
  // Probe on register_7_q
  // Probe on register_8_q
  // Probe on register_9_q
  // Probe on register_10_q
  // Probe on register_11_q
  // Probe on register_12_q
  // Probe on register_13_q
  // Probe on register_14_q
  // Probe on register_15_q
  // Probe on ReadReg1
  Multiplexer #(.select(2), .width(32), .enable("false")) multiplexer_1 (
    .in0({32{1'b0}}), .in1(register_1_q), .in2(register_2_q), .in3(register_3_q), .out(multiplexer_1_out),
    .sel(ReadReg1[1:0]));
  Multiplexer #(.select(2), .width(32), .enable("false")) multiplexer_2 (
    .in0(register_4_q), .in1(register_5_q), .in2(register_6_q), .in3(register_7_q), .out(multiplexer_2_out),
    .sel(ReadReg1[1:0]));
  Multiplexer #(.select(2), .width(32), .enable("false")) multiplexer_3 (
    .in0(register_8_q), .in1(register_9_q), .in2(register_10_q), .in3(register_11_q),
    .out(multiplexer_3_out), .sel(ReadReg1[1:0]));
  Multiplexer #(.select(2), .width(32), .enable("false")) multiplexer_4 (
    .in0(register_12_q), .in1(register_13_q), .in2(register_14_q), .in3(register_15_q),
    .out(multiplexer_4_out), .sel(ReadReg1[1:0]));
  // Probe on ReadReg2
  Multiplexer #(.select(2), .width(32), .enable("false")) multiplexer_5 (
    .in0({32{1'b0}}), .in1(register_1_q), .in2(register_2_q), .in3(register_3_q), .out(multiplexer_5_out),
    .sel(ReadReg2[1:0]));
  Multiplexer #(.select(2), .width(32), .enable("false")) multiplexer_6 (
    .in0(register_4_q), .in1(register_5_q), .in2(register_6_q), .in3(register_7_q), .out(multiplexer_6_out),
    .sel(ReadReg2[1:0]));
  Multiplexer #(.select(2), .width(32), .enable("false")) multiplexer_7 (
    .in0(register_8_q), .in1(register_9_q), .in2(register_10_q), .in3(register_11_q),
    .out(multiplexer_7_out), .sel(ReadReg2[1:0]));
  Multiplexer #(.select(2), .width(32), .enable("false")) multiplexer_8 (
    .in0(register_12_q), .in1(register_13_q), .in2(register_14_q), .in3(register_15_q),
    .out(multiplexer_8_out), .sel(ReadReg2[1:0]));
  Multiplexer #(.select(2), .width(32), .enable("false")) multiplexer_9 (
    .in0(multiplexer_5_out), .in1(multiplexer_6_out), .in2(multiplexer_7_out), .in3(multiplexer_8_out),
    .out(multiplexer_9_out), .sel(ReadReg2[3:2]));
  Multiplexer #(.select(2), .width(32), .enable("false")) multiplexer_10 (
    .in0(multiplexer_1_out), .in1(multiplexer_2_out), .in2(multiplexer_3_out), .in3(multiplexer_4_out),
    .out(multiplexer_10_out), .sel(ReadReg1[3:2]));
  Decoder #(.select(2), .disabled(0)) decoder_7 (
    .out0(decoder_7_out0), .out1(decoder_7_out1), .out2(decoder_7_out2), .out3(decoder_7_out3),
    .sel(WriteReg[3:2]), .en(decoder_1_out1));
  Decoder #(.select(2), .disabled(0)) decoder_8 (
    .out0(decoder_8_out0), .out1(decoder_8_out1), .out2(decoder_8_out2), .out3(decoder_8_out3),
    .sel(WriteReg[1:0]), .en(decoder_7_out0));
  Decoder #(.select(2), .disabled(0)) decoder_9 (
    .out0(decoder_9_out0), .out1(decoder_9_out1), .out2(decoder_9_out2), .out3(decoder_9_out3),
    .sel(WriteReg[1:0]), .en(decoder_7_out1));
  Decoder #(.select(2), .disabled(0)) decoder_10 (
    .out0(decoder_10_out0), .out1(decoder_10_out1), .out2(decoder_10_out2), .out3(decoder_10_out3),
    .sel(WriteReg[1:0]), .en(decoder_7_out2));
  Decoder #(.select(2), .disabled(0)) decoder_11 (
    .out0(decoder_11_out0), .out1(decoder_11_out1), .out2(decoder_11_out2), .out3(decoder_11_out3),
    .sel(WriteReg[1:0]), .en(decoder_7_out3));
  Register #(.width(32), .Select("low")) register_16 (
    .D(WriteData), .en(decoder_8_out0), .Q(register_16_q), .clk(Clk), .clr(Reset));
  Register #(.width(32), .Select("low")) register_17 (
    .D(WriteData), .en(decoder_8_out1), .Q(register_17_q), .clk(Clk), .clr(Reset), .preset(Reset));  // open: cs
  Register #(.width(32), .Select("low")) register_18 (
    .D(WriteData), .en(decoder_8_out2), .Q(register_18_q), .clk(Clk), .clr(Reset), .preset(Reset));  // open: cs
  Register #(.width(32), .Select("low")) register_19 (
    .D(WriteData), .en(decoder_8_out3), .Q(register_19_q), .clk(Clk), .clr(Reset), .preset(Reset));  // open: cs
  Register #(.width(32), .Select("low")) register_20 (
    .D(WriteData), .en(decoder_9_out0), .Q(register_20_q), .clk(Clk), .clr(Reset), .preset(Reset));  // open: cs
  Register #(.width(32), .Select("low")) register_21 (
    .D(WriteData), .en(decoder_9_out1), .Q(register_21_q), .clk(Clk), .clr(Reset), .preset(Reset));  // open: cs
  Register #(.width(32), .Select("low")) register_22 (
    .D(WriteData), .en(decoder_9_out2), .Q(register_22_q), .clk(Clk), .clr(Reset), .preset(Reset));  // open: cs
  Register #(.width(32), .Select("low")) register_23 (
    .D(WriteData), .en(decoder_9_out3), .Q(register_23_q), .clk(Clk), .clr(Reset), .preset(Reset));  // open: cs
  Register #(.width(32), .Select("low")) register_24 (
    .D(WriteData), .en(decoder_10_out0), .Q(register_24_q), .clk(Clk), .clr(Reset), .preset(Reset));  // open: cs
  Register #(.width(32), .Select("low")) register_25 (
    .D(WriteData), .en(decoder_10_out1), .Q(register_25_q), .clk(Clk), .clr(Reset), .preset(Reset));  // open: cs
  Register #(.width(32), .Select("low")) register_26 (
    .D(WriteData), .en(decoder_10_out2), .Q(register_26_q), .clk(Clk), .clr(Reset), .preset(Reset));  // open: cs
  Register #(.width(32), .Select("low")) register_27 (
    .D(WriteData), .en(decoder_10_out3), .Q(register_27_q), .clk(Clk), .clr(Reset), .preset(Reset));  // open: cs
  Register #(.width(32), .Select("low")) register_28 (
    .D(WriteData), .en(decoder_11_out0), .Q(register_28_q), .clk(Clk), .clr(Reset), .preset(Reset));  // open: cs
  Register #(.width(32), .Select("low")) register_29 (
    .D(WriteData), .en(decoder_11_out1), .Q(register_29_q), .clk(Clk), .clr(Reset), .preset(Reset));  // open: cs
  Register #(.width(32), .Select("low")) register_30 (
    .D(WriteData), .en(decoder_11_out2), .Q(register_30_q), .clk(Clk), .clr(Reset), .preset(Reset));  // open: cs
  Register #(.width(32), .Select("low")) register_31 (
    .D(WriteData), .en(decoder_11_out3), .Q(register_31_q), .clk(Clk), .clr(Reset), .preset(Reset));  // open: cs
  // Probe on register_16_q
  // Probe on register_17_q
  // Probe on register_18_q
  // Probe on register_19_q
  // Probe on register_20_q
  // Probe on register_21_q
  // Probe on register_22_q
  // Probe on register_23_q
  // Probe on register_24_q
  // Probe on register_25_q
  // Probe on register_26_q
  // Probe on register_27_q
  // Probe on register_28_q
  // Probe on register_29_q
  // Probe on register_30_q
  // Probe on register_31_q
  Multiplexer #(.width(32), .enable("false")) multiplexer_11 (
    .in0(multiplexer_10_out), .in1(multiplexer_22_out), .out(ReadData1), .sel(ReadReg1[4]));
  Multiplexer #(.width(32), .enable("false")) multiplexer_12 (
    .in0(multiplexer_9_out), .in1(multiplexer_21_out), .out(ReadData2), .sel(ReadReg2[4]));
  Multiplexer #(.select(2), .width(32), .enable("false")) multiplexer_13 (
    .in0(register_16_q), .in1(register_17_q), .in2(register_18_q), .in3(register_19_q),
    .out(multiplexer_13_out), .sel(ReadReg1[1:0]));
  Multiplexer #(.select(2), .width(32), .enable("false")) multiplexer_14 (
    .in0(register_20_q), .in1(register_21_q), .in2(register_22_q), .in3(register_23_q),
    .out(multiplexer_14_out), .sel(ReadReg1[1:0]));
  Multiplexer #(.select(2), .width(32), .enable("false")) multiplexer_15 (
    .in0(register_24_q), .in1(register_25_q), .in2(register_26_q), .in3(register_27_q),
    .out(multiplexer_15_out), .sel(ReadReg1[1:0]));
  Multiplexer #(.select(2), .width(32), .enable("false")) multiplexer_16 (
    .in0(register_28_q), .in1(register_29_q), .in2(register_30_q), .in3(register_31_q),
    .out(multiplexer_16_out), .sel(ReadReg1[1:0]));
  Multiplexer #(.select(2), .width(32), .enable("false")) multiplexer_17 (
    .in0(register_16_q), .in1(register_17_q), .in2(register_18_q), .in3(register_19_q),
    .out(multiplexer_17_out), .sel(ReadReg2[1:0]));
  Multiplexer #(.select(2), .width(32), .enable("false")) multiplexer_18 (
    .in0(register_20_q), .in1(register_21_q), .in2(register_22_q), .in3(register_23_q),
    .out(multiplexer_18_out), .sel(ReadReg2[1:0]));
  Multiplexer #(.select(2), .width(32), .enable("false")) multiplexer_19 (
    .in0(register_24_q), .in1(register_25_q), .in2(register_26_q), .in3(register_27_q),
    .out(multiplexer_19_out), .sel(ReadReg2[1:0]));
  Multiplexer #(.select(2), .width(32), .enable("false")) multiplexer_20 (
    .in0(register_28_q), .in1(register_29_q), .in2(register_30_q), .in3(register_31_q),
    .out(multiplexer_20_out), .sel(ReadReg2[1:0]));
  Multiplexer #(.select(2), .width(32), .enable("false")) multiplexer_21 (
    .in0(multiplexer_17_out), .in1(multiplexer_18_out), .in2(multiplexer_19_out), .in3(multiplexer_20_out),
    .out(multiplexer_21_out), .sel(ReadReg2[3:2]));
  Multiplexer #(.select(2), .width(32), .enable("false")) multiplexer_22 (
    .in0(multiplexer_13_out), .in1(multiplexer_14_out), .in2(multiplexer_15_out), .in3(multiplexer_16_out),
    .out(multiplexer_22_out), .sel(ReadReg1[3:2]));
endmodule

module next_pc_sel (
  input  b,
  input  j,
  input  jr,
  output [1:0] out_4
);

  wire and_1_out, and_2_out, and_3_out, and_4_out, not_1_out, not_2_out, not_3_out, not_4_out, not_5_out,
       not_6_out, not_7_out, not_8_out;

  not not_1 (not_1_out, b);
  not not_2 (not_2_out, j);
  not not_3 (not_3_out, b);
  not not_4 (not_4_out, jr);
  not not_5 (not_5_out, b);
  not not_6 (not_6_out, j);
  not not_7 (not_7_out, j);
  not not_8 (not_8_out, jr);
  and and_1 (and_1_out, not_1_out, not_2_out, jr);
  and and_2 (and_2_out, not_3_out, j, not_4_out);
  and and_3 (and_3_out, not_5_out, not_6_out, jr);
  and and_4 (and_4_out, b, not_7_out, not_8_out);
  or or_1 (out_4[1], and_1_out, and_2_out);
  or or_2 (out_4[0], and_3_out, and_4_out);

  // Notes on the sheet:
  //   next_pc_select
endmodule

module operand_A_sel (
  input  LUI,
  input  JALR,
  input  JAL,
  output [1:0] out_4
);

  wire and_1_out, and_2_out, and_3_out, not_1_out, not_2_out, not_3_out, not_4_out, not_5_out, not_6_out,
       not_7_out, not_8_out;

  not not_1 (not_1_out, LUI);
  not not_2 (not_2_out, JALR);
  not not_3 (not_3_out, LUI);
  not not_4 (not_4_out, JAL);
  not not_5 (not_5_out, JALR);
  not not_6 (not_6_out, JAL);
  not not_7 (not_7_out, JALR);
  not not_8 (not_8_out, JAL);
  and and_1 (and_1_out, not_1_out, not_2_out, JAL);
  and and_2 (and_2_out, not_3_out, JALR, not_4_out);
  and and_3 (and_3_out, LUI, not_5_out, not_6_out);
  and and_4 (out_4[0], LUI, not_7_out, not_8_out);
  or or_1 (out_4[1], and_1_out, and_2_out, and_3_out);

  // Notes on the sheet:
  //   IF WE ADD "AUIPC" INSTRUCTION THEN OUTPUT MUST BE "01"
endmodule

module Immediate_Generation (
  input  [31:0] in_1,
  input  [31:0] in_2,
  output [31:0] out_3,
  output [31:0] out_4,
  output [31:0] out_5,
  output [31:0] out_6,
  output [31:0] out_7
);

  wire [11:11] undriven;
  wire [31:0] bit_extender_1_out, bit_extender_4_out, bit_extender_5_out;

  assign bit_extender_1_out = {{12{in_1[31]}}, in_1[31:12]};  // Bit_Extender bit_extender_1
  assign out_3 = {{20{1'b0}}, {in_1[31:25], in_1[11:7]}};  // Bit_Extender bit_extender_2
  Shifter #(.width(32)) shifter_1 (.in(bit_extender_1_out), .\dist (5'b01100), .out(out_5));
  assign out_7 = {{20{1'b0}}, in_1[31:20]};  // Bit_Extender bit_extender_3
  assign bit_extender_4_out = {{19{1'b0}}, {in_1[31], in_1[7], in_1[30:25], in_1[11:8], 1'b0}};  // Bit_Extender bit_extender_4
  assign bit_extender_5_out = {{11{1'b0}}, {in_1[31], in_1[19:12], undriven[11], in_1[30:21], 1'b0}};  // Bit_Extender bit_extender_5
  Adder #(.width(32)) adder_1 (.a(bit_extender_4_out), .b(in_2), .out(out_4));  // open: cin, cout
  Adder #(.width(32)) adder_2 (.a(in_2), .b(bit_extender_5_out), .out(out_6));  // open: cin, cout

  // Notes on the sheet:
  //   INSTRUCTION
  //   PC
  //   S-Immediate
  //   SB-Immediate
  //   U-Immediate
  //   UJ-type
  //   I-Immediate
endmodule

module JALR_target (
  input  [31:0] in_1,
  input  [31:0] in_2,
  output [31:0] out_3
);

  wire [31:0] adder_1_out;

  Adder #(.width(32)) adder_1 (.a(in_1), .b(in_2), .out(adder_1_out));  // open: cin, cout
  assign out_3 = 32'hfffffffe & adder_1_out;  // AND_Gate and_1, 32 bits wide

  // Notes on the sheet:
  //   JALR Target
  //   AND GATE,CONSTANT
endmodule

module ALUop (
  input  R_Type,
  input  Load,
  input  Store,
  input  Branch,
  input  I_Type,
  input  JALR,
  input  JAL,
  input  LUI,
  output [2:0] out_9
);

  wire not_1_out, not_2_out, not_3_out, not_4_out, not_5_out, not_6_out, not_7_out, not_8_out, not_9_out,
       not_10_out, not_11_out, not_12_out, not_13_out;

  not not_1 (not_1_out, R_Type);
  not not_2 (not_2_out, Branch);
  not not_3 (not_3_out, I_Type);
  not not_4 (not_4_out, JALR);
  not not_5 (not_5_out, JAL);
  not not_6 (not_6_out, R_Type);
  not not_7 (not_7_out, Load);
  not not_8 (not_8_out, Store);
  not not_9 (not_9_out, I_Type);
  not not_10 (not_10_out, R_Type);
  not not_11 (not_11_out, Load);
  not not_12 (not_12_out, Branch);
  not not_13 (not_13_out, LUI);
  and and_1 (out_9[2], not_1_out, not_2_out, not_3_out, not_4_out, not_5_out);
  and and_2 (out_9[1], not_6_out, not_7_out, not_8_out, not_9_out);
  and and_3 (out_9[0], not_10_out, not_11_out, not_12_out, not_13_out);
endmodule

module Pipeline_Fetch (
  input  [31:0] in_1,
  input  [31:0] in_2,
  input  [31:0] in_3,
  input  in_4,
  output [31:0] out_5,
  output [31:0] out_6,
  output [31:0] out_7
);

  Register #(.width(32), .Select("low")) register_1 (.D(in_1), .Q(out_5), .clk(in_4));  // open: en, clr
  Register #(.width(32), .Select("low")) register_2 (.D(in_2), .Q(out_6), .clk(in_4));  // open: en, clr
  Register #(.width(32), .Select("low")) register_3 (.D(in_3), .Q(out_7), .clk(in_4));  // open: en, clr
endmodule

module Pipeline_Decode (
  input  [31:0] in_1,
  input  [31:0] PC,
  input  [31:0] Instruction,
  input  in_4,
  output [31:0] out_5,
  output [31:0] out_6,
  output [31:0] out_7
);

  Register #(.width(32), .Select("low")) register_1 (.D(in_1), .Q(out_5), .clk(in_4));  // open: en, clr
  Register #(.width(32), .Select("low")) register_2 (.D(PC), .Q(out_6), .clk(in_4));  // open: en, clr
  Register #(.width(32), .Select("low")) register_3 (.D(Instruction), .Q(out_7), .clk(in_4));  // open: en, clr
endmodule
